// Logisim project vendingmachine.circ as structural Verilog: 1 circuit, main circuit main
module main (
  input  TURNON
);

  wire and_1_out, and_2_out, and_3_out, and_4_out, and_6_out, and_7_out, and_8_out, and_10_out, and_11_out,
       and_12_out, and_13_out, and_14_out, and_15_out, and_16_out, buffer_1_out, buffer_2_out, F_out,
       j_k_ff_1_q, j_k_ff_1_qn, j_k_ff_2_q, j_k_ff_2_qn, j_k_ff_3_q, j_k_ff_3_qn, not_1_out, not_2_out,
       not_4_out, not_5_out, or_1_out, or_2_out, or_3_out, or_4_out, or_5_out, S_out;

  Button F (.out(F_out));
  Button S (.out(S_out));
  and and_1 (and_1_out, j_k_ff_1_qn, TURNON);
  not not_1 (not_1_out, TURNON);
  and and_2 (and_2_out, j_k_ff_1_q, S_out);
  and and_3 (and_3_out, not_1_out, j_k_ff_1_q);
  or or_1 (or_1_out, j_k_ff_1_qn, TURNON);
  or or_2 (or_2_out, j_k_ff_2_q, j_k_ff_3_q);
  or or_3 (or_3_out, or_2_out, j_k_ff_1_q);
  J_K_Flip_Flop j_k_ff_1 (
    .J(and_1_out), .K(and_3_out), .clk(F_out), .Q(j_k_ff_1_q), .Qn(j_k_ff_1_qn), .reset(or_5_out));  // open: preset
  and and_4 (and_4_out, or_1_out, j_k_ff_2_q);
  and and_5 (or_3_out, j_k_ff_2_qn, j_k_ff_1_q, j_k_ff_3_qn, F_out);
  not not_2 (not_2_out, or_3_out);
  LED FA (.in(not_2_out));
  buf buffer_1 (buffer_1_out, j_k_ff_1_q);
  LED A0 (.in(buffer_1_out));
  not not_3 (buffer_1_out, j_k_ff_2_q);
  J_K_Flip_Flop j_k_ff_2 (
    .J(and_8_out), .K(and_4_out), .clk(F_out), .Q(j_k_ff_2_q), .Qn(j_k_ff_2_qn), .reset(or_5_out));  // open: preset
  and and_6 (and_6_out, j_k_ff_1_q, j_k_ff_2_qn);
  not not_4 (not_4_out, or_2_out);
  LED FB (.in(not_4_out));
  and and_7 (and_7_out, j_k_ff_2_q, S_out);
  LED B0 (.in(j_k_ff_2_q));
  and and_8 (and_8_out, and_6_out, TURNON);
  and and_9 (or_2_out, j_k_ff_1_q, j_k_ff_2_q, F_out, j_k_ff_3_qn);
  not not_5 (not_5_out, buffer_2_out);
  and and_10 (and_10_out, j_k_ff_3_q, TURNON);
  and and_11 (and_11_out, j_k_ff_1_q, j_k_ff_2_q);
  or or_4 (or_4_out, j_k_ff_1_qn, j_k_ff_2_qn);
  and and_12 (and_12_out, j_k_ff_1_q, j_k_ff_2_qn, j_k_ff_3_q, F_out);
  buf buffer_2 (buffer_2_out, and_12_out);
  LED FC (.in(not_5_out));
  and and_13 (and_13_out, j_k_ff_3_qn, and_11_out);
  J_K_Flip_Flop j_k_ff_3 (
    .J(and_13_out), .K(and_14_out), .clk(F_out), .Q(j_k_ff_3_q), .Qn(j_k_ff_3_qn), .reset(and_16_out));  // open: preset
  and and_14 (and_14_out, j_k_ff_3_q, or_4_out);
  or or_5 (or_5_out, and_2_out, and_10_out, and_7_out);
  and and_15 (and_15_out, j_k_ff_3_q, j_k_ff_1_q);
  and and_16 (and_16_out, and_15_out, and_12_out);
  // also tied to VCC on the sheet: {not_2_out, not_4_out, not_5_out}
endmodule
